// Logisim project Visto_1a.circ as structural Verilog: 1 circuit, main circuit main
module main (
  input  C,
  input  B,
  input  A,
  output X
);

  wire not_1_out;

  not not_1 (not_1_out, C);
  Multiplexer #(.select(2), .enable("false")) multiplexer_1 (
    .in0(1'b0), .in1(not_1_out), .in2(C), .in3(1'b1), .out(X), .sel({A, B}));
endmodule
